// Logisim project MeioSomador_1bit.circ as structural Verilog: 1 circuit, main circuit main
module main (
  input  A0,
  input  B0,
  output S0,
  output CO
);

  xor xor_1 (S0, A0, B0);
  and and_1 (CO, A0, B0);
endmodule
