// Logisim project ULA.circ as structural Verilog: 4 circuits, main circuit main
module main (
  input  in_1,
  input  in_2,
  input  in_3,
  input  in_4,
  input  in_5,
  input  in_6,
  input  in_7,
  input  in_8,
  input  [1:0] in_9,
  output out_10,
  output out_11,
  output out_12,
  output out_13,
  output out_14
);

  wire ula_1_out_7, ula_2_out_7, ula_3_out_7;

  ULA ula_1 (
    .in_2(in_1), .in_3(in_2), .in_1(1'b0), .out_7(ula_1_out_7), .in_4(in_9[1]), .in_5(in_9[0]), .out_6(out_13));
  ULA ula_2 (
    .in_2(in_3), .in_3(in_4), .in_1(ula_1_out_7), .out_7(ula_2_out_7), .in_4(in_9[1]), .in_5(in_9[0]),
    .out_6(out_12));
  ULA ula_3 (
    .in_2(in_5), .in_3(in_6), .in_1(ula_2_out_7), .out_7(ula_3_out_7), .in_4(in_9[1]), .in_5(in_9[0]),
    .out_6(out_11));
  ULA ula_4 (
    .in_2(in_7), .in_3(in_8), .in_1(ula_3_out_7), .out_7(out_14), .in_4(in_9[1]), .in_5(in_9[0]),
    .out_6(out_10));

  // Notes on the sheet:
  //   00 -  AND /   01 - OR / 10 - NOT A / 11 - Soma
endmodule

module Somador (
  input  in_1,
  input  in_2,
  input  in_3,
  output out_4,
  output out_5
);

  wire and_1_out, and_2_out, xor_1_out;

  xor xor_1 (xor_1_out, in_2, in_3);
  and and_1 (and_1_out, in_2, in_3);
  xor xor_2 (out_4, in_1, xor_1_out);
  and and_2 (and_2_out, in_1, xor_1_out);
  or or_1 (out_5, and_1_out, and_2_out);
endmodule

module Multiplexador (
  input  in_1,
  input  in_2,
  input  in_3,
  input  in_4,
  input  in_5,
  input  in_6,
  output out_7
);

  wire and_1_out, and_2_out, and_3_out, and_4_out, and_5_out, and_6_out, and_7_out, and_8_out, not_1_out,
       not_2_out, not_3_out, not_4_out, or_1_out, or_2_out;

  and and_1 (and_1_out, in_1, not_1_out);
  not not_1 (not_1_out, in_6);
  not not_2 (not_2_out, in_5);
  not not_3 (not_3_out, in_5);
  not not_4 (not_4_out, in_6);
  and and_2 (and_2_out, and_1_out, not_2_out);
  and and_3 (and_3_out, in_2, not_3_out);
  and and_4 (and_4_out, and_3_out, in_6);
  and and_5 (and_5_out, in_3, in_5);
  and and_6 (and_6_out, and_5_out, not_4_out);
  and and_7 (and_7_out, in_4, in_5);
  and and_8 (and_8_out, and_7_out, in_6);
  or or_1 (or_1_out, and_2_out, and_4_out);
  or or_2 (or_2_out, and_6_out, and_8_out);
  or or_3 (out_7, or_1_out, or_2_out);
endmodule

module ULA (
  input  in_1,
  input  in_2,
  input  in_3,
  input  in_4,
  input  in_5,
  output out_6,
  output out_7
);

  wire and_1_out, not_1_out, or_1_out, somador_1_out_4;

  and and_1 (and_1_out, in_2, in_3);
  or or_1 (or_1_out, in_2, in_3);
  not not_1 (not_1_out, in_2);
  Somador somador_1 (.in_2(in_2), .in_3(in_3), .in_1(in_1), .out_5(out_7), .out_4(somador_1_out_4));
  Multiplexador multiplexador_1 (
    .in_1(and_1_out), .in_2(or_1_out), .in_3(not_1_out), .in_4(somador_1_out_4), .in_5(in_4), .in_6(in_5),
    .out_7(out_6));
endmodule
